// Logisim project Moris_Mano_Basic_Computer.circ as structural Verilog
// T1
module main (
  input  [7:0] INP,
  output [2:0] out_2,
  output [15:0] out_3,
  output [15:0] out_4,
  output [15:0] out_5,
  output [15:0] out_6,
  output [15:0] out_7,
  output [15:0] out_8,
  output out_9,
  output out_10,
  output [6:0] out_11,
  output [15:0] out_12,
  output [15:0] out_13,
  output [15:0] out_14,
  output [15:0] out_15,
  output [7:0] out_16
);

  wire ac_cntrl_1_clr_ac, ac_cntrl_1_inr_ac, ac_cntrl_1_ld_ac, and_2_out, and_3_out, ar_cntrl_1_clr_ar,
       ar_cntrl_1_inr_ar, ar_cntrl_1_ld_ar, CLK, clock_1_out, dr_cntrl_1_inr, dr_cntrl_1_load, FGI, FGO,
       i_1_i, IEN, IR_15, m_cntrl_1_m_rd, m_cntrl_1_m_wr, not_1_out, out_cntrl_1_load, pc_cntrl1_1_clr,
       pc_cntrl1_1_inr, pc_cntrl1_1_ld, R, s_1_s;
  wire [3:0] T4bit;
  wire [7:0] INP_t;

  S s_1 (.IR(out_14), .T3(out_5[3]), .I(out_14[15]), .S(s_1_s), .ClK(CLK));
  not not_1 (not_1_out, FGI);
  Clock clock_1 (.out(clock_1_out));
  Register register_1 (.D(INP), .en(not_1_out), .Q(INP_t));  // open: clk, clr
  and and_1 (CLK, clock_1_out, ~s_1_s);  // AND_Gate
  ALU alu_1 (.CNTRL(out_11), .AC(out_13), .INP(INP_t), .DR(out_8), .E(out_10), .TO_AC(out_12), .E_OUT(out_9));
  and and_2 (and_2_out, ~R, out_5[1]);  // AND_Gate
  and and_3 (and_3_out, R, out_5[0]);
  SC_CNTRL sc_cntrl_1 (.R(R), .IR(out_14), .I(out_14[15]), .CLK(CLK), .out_5(out_5), .out_6(T4bit));
  AR_CNTRL ar_cntrl_1 (
    .IR(out_14), .I(out_14[15]), .R(R), .T(out_5), .LD_AR(ar_cntrl_1_ld_ar), .INR_AR(ar_cntrl_1_inr_ar),
    .CLR_AR(ar_cntrl_1_clr_ar));
  DR_CNTRL dr_cntrl_1 (
    .T4(out_5[4]), .T5(out_5[5]), .IR(out_14), .T3(out_5[3]), .I(out_14[15]), .LOAD(dr_cntrl_1_load),
    .INR(dr_cntrl_1_inr));
  AC_CNTRL ac_cntrl_1 (
    .in_1(out_5[5]), .IR(out_14), .T3(out_5[3]), .I(out_14[15]), .LD_AC(ac_cntrl_1_ld_ac), .CTRL(out_11),
    .INR_AC(ac_cntrl_1_inr_ac), .CLR_AC(ac_cntrl_1_clr_ac));
  OUT_CNTRL out_cntrl_1 (.IR(out_14), .T3(out_5[3]), .I(out_14[15]), .LOAD(out_cntrl_1_load));
  PC_CNTRL1 pc_cntrl1_1 (
    .DR(out_8), .IR(out_14), .AC(out_13), .INR(pc_cntrl1_1_inr), .I(out_14[15]), .CLR(pc_cntrl1_1_clr),
    .E(out_10), .FGI(FGI), .LD(pc_cntrl1_1_ld), .FGO(FGO), .R(R), .T(out_5));
  M_CNTRL m_cntrl_1 (.IR(out_14), .I(out_14[15]), .R(R), .M_WR(m_cntrl_1_m_wr), .M_RD(m_cntrl_1_m_rd), .in_4(T4bit));
  AR ar_1 (
    .INP(out_6), .out_6(out_4), .CLR(ar_cntrl_1_clr_ar), .INC(ar_cntrl_1_inr_ar), .CLK(CLK),
    .LOAD(ar_cntrl_1_ld_ar));
  PC pc_1 (.in_2(out_6), .out_6(out_7), .CLR(pc_cntrl1_1_clr), .LOAD(pc_cntrl1_1_ld), .INC(pc_cntrl1_1_inr), .CLK(CLK));
  BASE_REGISTER base_register_1 (
    .in_2(out_6), .out_6(out_8), .CLR(1'b0), .LOAD(dr_cntrl_1_load), .INC(dr_cntrl_1_inr), .CLK(CLK));
  BASE_REGISTER base_register_2 (
    .in_2(out_12), .out_6(out_13), .CLR(ac_cntrl_1_clr_ac), .LOAD(ac_cntrl_1_ld_ac), .INC(ac_cntrl_1_inr_ac),
    .CLK(CLK));
  BASE_REGISTER base_register_3 (.in_2(out_6), .out_6(out_14), .CLR(1'b0), .LOAD(and_2_out), .INC(1'b0), .CLK(CLK));
  BASE_REGISTER base_register_4 (.in_2(out_6), .out_6(out_15), .CLR(1'b0), .LOAD(and_3_out), .INC(1'b0), .CLK(CLK));
  OUTR outr_1 (.INPUT(out_6), .OUTPUT(out_16), .ClK(CLK), .LD_OUTR(out_cntrl_1_load));
  I i_1 (.Clock(CLK), .IR_15(IR_15), .R(R), .TIME(out_5), .I(i_1_i));
  S s_2 (.IR(out_14), .T3(out_5[3]), .I(out_14[15]), .ClK(CLK));  // open: S
  E e_1 (.E_OUT_ALU(out_9), .IR(out_14), .T3(out_5[3]), .I(out_14[15]), .Clock(CLK), .E(out_10));
  RAM #(.addrWidth(12), .dataWidth(16), .bus("separate")) ram_1 (
    .addr(out_4[11:0]), .din(out_6), .data(out_3), .str(m_cntrl_1_m_wr), .clk(CLK), .ld(m_cntrl_1_m_rd));  // open: sel, clr
  FGI fgi_1 (.IR(out_14), .T3(out_5[3]), .I(out_14[15]), .INPR(INP_t), .FGI(FGI), .ClK(CLK));
  R r_1 (.FGO(FGO), .FGI(FGI), .IEN(IEN), .TIME(out_5), .R(R), .Clock(CLK));
  BUS_CNTRL bus_cntrl_1 (.IR(out_14), .I(out_14[15]), .R(R), .T(out_5), .Select(out_2));
  FGO fgo_1 (.IR(out_14), .T3(out_5[3]), .I(out_14[15]), .OUTR(out_16), .FGO(FGO), .ClK(CLK));
  IEN ien_1 (.IR(out_14), .ClK(CLK), .R(R), .T3(out_5[3]), .I(out_14[15]));  // open: T2, IEN
  bus bus_1 (
    .AR(out_4), .PC(out_7), .DR(out_8), .AC(out_13), .IR(out_14), .TR(out_15), .M(out_3), .SELECT(out_2),
    .out_9(out_6));

  // Other names for the same wires on the sheet: AC[15:0] = out_13; DR[15:0] = out_8; E = out_10; EAO = out_9;
  //   IR[15:0] = out_14; I = out_14[15]; OUUTR[7:0] = out_16; T[15:0] = out_5; T0 = out_5[0]; T1 = out_5[1];
  //   T2 = out_5[2]; T3 = out_5[3]; T4 = out_5[4]; T5 = out_5[5]
endmodule

module full_adder (
  input  x,
  input  y,
  input  cIn,
  output s,
  output cout
);

  wire and_1_out, and_2_out, xor_1_out;

  xor xor_1 (xor_1_out, x, y);
  xor xor_2 (s, xor_1_out, cIn);
  and and_1 (and_1_out, xor_1_out, cIn);
  and and_2 (and_2_out, x, y);
  or or_1 (cout, and_1_out, and_2_out);
endmodule

module bus (
  input  [15:0] AR,
  input  [15:0] PC,
  input  [15:0] DR,
  input  [15:0] AC,
  input  [15:0] IR,
  input  [15:0] TR,
  input  [15:0] M,
  input  [2:0] SELECT,
  output [15:0] out_9
);

  Multiplexer #(.select(3), .width(16)) multiplexer_1 (
    .in0({16{1'b0}}), .in1(AR), .in2(PC), .in3(DR), .in4(AC), .in5(IR), .in6(TR), .in7(M), .out(out_9),
    .sel(SELECT));  // open: en
endmodule

module AR (
  input  LOAD,
  input  [15:0] INP,
  input  INC,
  input  CLR,
  input  CLK,
  output [15:0] out_6
);

  Counter #(.width(12), .max('hfff)) counter_1 (
    .load(LOAD), .D(INP[11:0]), .count(INC), .Q(out_6[11:0]), .clk(CLK), .clr(CLR));  // open: carry

  assign out_6[15:12] = 4'b0000;
endmodule

module PC (
  input  LOAD,
  input  [15:0] in_2,
  input  INC,
  input  CLR,
  input  CLK,
  output [15:0] out_6
);

  Counter #(.width(12), .max('hfff)) counter_1 (
    .load(LOAD), .D(in_2[11:0]), .count(INC), .Q(out_6[11:0]), .clk(CLK), .clr(CLR));  // open: carry

  assign out_6[15:12] = 4'b0000;
endmodule

module BASE_REGISTER (
  input  LOAD,
  input  [15:0] in_2,
  input  INC,
  input  CLR,
  input  CLK,
  output [15:0] out_6
);

  Counter #(.width(16), .max('hffff)) counter_1 (
    .load(LOAD), .D(in_2), .count(INC), .Q(out_6), .clk(CLK), .clr(CLR));  // open: carry
endmodule

module ALU (
  input  [6:0] CNTRL,
  input  [15:0] AC,
  input  [7:0] INP,
  input  [15:0] DR,
  input  E,
  output [15:0] TO_AC,
  output E_OUT
);

  wire and_1_out, and_2_out, and_3_out, and_4_out, CARRY_OUT, CRY7, one_bit_alu_1_c_2, one_bit_alu_2_c_2,
       one_bit_alu_3_c_2, one_bit_alu_4_c_2, one_bit_alu_5_c_2, one_bit_alu_6_c_2, one_bit_alu_7_c_2,
       one_bit_alu_9_c_2, one_bit_alu_10_c_2, one_bit_alu_11_c_2, one_bit_alu_12_c_2, one_bit_alu_13_c_2,
       one_bit_alu_14_c_2, one_bit_alu_15_c_2, or_1_out;

  or or_1 (or_1_out, CNTRL[0], CNTRL[6], CNTRL[5]);
  and and_1 (and_1_out, CARRY_OUT, CNTRL[0]);
  and and_2 (and_2_out, CNTRL[5], AC[0]);
  and and_3 (and_3_out, CNTRL[6], AC[15]);
  and and_4 (and_4_out, E, ~or_1_out);  // AND_Gate
  or or_2 (E_OUT, and_1_out, and_2_out, and_3_out, and_4_out);
  ONE_BIT_ALU one_bit_alu_1 (
    .CNTRL({CNTRL[0], CNTRL[1], CNTRL[2], CNTRL[3], CNTRL[4], CNTRL[5], CNTRL[6]}), .C_2(one_bit_alu_1_c_2),
    .I(TO_AC[0]), .INPR(INP[0]), .DR(DR[0]), .AC_i(AC[0]), .AC_i_1(E), .AC_i_1_2(AC[1]), .C(1'b0));
  ONE_BIT_ALU one_bit_alu_2 (
    .CNTRL({CNTRL[0], CNTRL[1], CNTRL[2], CNTRL[3], CNTRL[4], CNTRL[5], CNTRL[6]}), .C_2(one_bit_alu_2_c_2),
    .I(TO_AC[1]), .INPR(INP[1]), .DR(DR[1]), .AC_i(AC[1]), .AC_i_1(AC[0]), .AC_i_1_2(AC[2]),
    .C(one_bit_alu_1_c_2));
  ONE_BIT_ALU one_bit_alu_3 (
    .CNTRL({CNTRL[0], CNTRL[1], CNTRL[2], CNTRL[3], CNTRL[4], CNTRL[5], CNTRL[6]}), .C_2(one_bit_alu_3_c_2),
    .I(TO_AC[2]), .INPR(INP[2]), .DR(DR[2]), .AC_i(AC[2]), .AC_i_1(AC[1]), .AC_i_1_2(AC[3]),
    .C(one_bit_alu_2_c_2));
  ONE_BIT_ALU one_bit_alu_4 (
    .CNTRL({CNTRL[0], CNTRL[1], CNTRL[2], CNTRL[3], CNTRL[4], CNTRL[5], CNTRL[6]}), .C_2(one_bit_alu_4_c_2),
    .I(TO_AC[3]), .INPR(INP[3]), .DR(DR[3]), .AC_i(AC[3]), .AC_i_1(AC[2]), .AC_i_1_2(AC[4]),
    .C(one_bit_alu_3_c_2));
  ONE_BIT_ALU one_bit_alu_5 (
    .CNTRL({CNTRL[0], CNTRL[1], CNTRL[2], CNTRL[3], CNTRL[4], CNTRL[5], CNTRL[6]}), .C_2(one_bit_alu_5_c_2),
    .I(TO_AC[4]), .INPR(INP[4]), .DR(DR[4]), .AC_i(AC[4]), .AC_i_1(AC[3]), .AC_i_1_2(AC[5]),
    .C(one_bit_alu_4_c_2));
  ONE_BIT_ALU one_bit_alu_6 (
    .CNTRL({CNTRL[0], CNTRL[1], CNTRL[2], CNTRL[3], CNTRL[4], CNTRL[5], CNTRL[6]}), .C_2(one_bit_alu_6_c_2),
    .I(TO_AC[5]), .INPR(INP[5]), .DR(DR[5]), .AC_i(AC[5]), .AC_i_1(AC[4]), .AC_i_1_2(AC[6]),
    .C(one_bit_alu_5_c_2));
  ONE_BIT_ALU one_bit_alu_7 (
    .CNTRL({CNTRL[0], CNTRL[1], CNTRL[2], CNTRL[3], CNTRL[4], CNTRL[5], CNTRL[6]}), .C_2(one_bit_alu_7_c_2),
    .I(TO_AC[6]), .INPR(INP[6]), .DR(DR[6]), .AC_i(AC[6]), .AC_i_1(AC[5]), .AC_i_1_2(AC[7]),
    .C(one_bit_alu_6_c_2));
  ONE_BIT_ALU one_bit_alu_8 (
    .CNTRL({CNTRL[0], CNTRL[1], CNTRL[2], CNTRL[3], CNTRL[4], CNTRL[5], CNTRL[6]}), .C_2(CRY7), .I(TO_AC[7]),
    .INPR(INP[7]), .DR(DR[7]), .AC_i(AC[7]), .AC_i_1(AC[6]), .AC_i_1_2(AC[8]), .C(one_bit_alu_7_c_2));
  ONE_BIT_ALU one_bit_alu_9 (
    .CNTRL({CNTRL[0], CNTRL[1], CNTRL[2], CNTRL[3], CNTRL[4], CNTRL[5], CNTRL[6]}), .C_2(one_bit_alu_9_c_2),
    .I(TO_AC[8]), .INPR(1'b0), .DR(DR[8]), .AC_i(AC[8]), .AC_i_1(AC[7]), .AC_i_1_2(AC[9]), .C(CRY7));
  ONE_BIT_ALU one_bit_alu_10 (
    .CNTRL({CNTRL[0], CNTRL[1], CNTRL[2], CNTRL[3], CNTRL[4], CNTRL[5], CNTRL[6]}), .C_2(one_bit_alu_10_c_2),
    .I(TO_AC[9]), .INPR(1'b0), .DR(DR[9]), .AC_i(AC[9]), .AC_i_1(AC[8]), .AC_i_1_2(AC[10]),
    .C(one_bit_alu_9_c_2));
  ONE_BIT_ALU one_bit_alu_11 (
    .CNTRL({CNTRL[0], CNTRL[1], CNTRL[2], CNTRL[3], CNTRL[4], CNTRL[5], CNTRL[6]}), .C_2(one_bit_alu_11_c_2),
    .I(TO_AC[10]), .INPR(1'b0), .DR(DR[10]), .AC_i(AC[10]), .AC_i_1(AC[9]), .AC_i_1_2(AC[11]),
    .C(one_bit_alu_10_c_2));
  ONE_BIT_ALU one_bit_alu_12 (
    .CNTRL({CNTRL[0], CNTRL[1], CNTRL[2], CNTRL[3], CNTRL[4], CNTRL[5], CNTRL[6]}), .C_2(one_bit_alu_12_c_2),
    .I(TO_AC[11]), .INPR(1'b0), .DR(DR[11]), .AC_i(AC[11]), .AC_i_1(AC[10]), .AC_i_1_2(AC[12]),
    .C(one_bit_alu_11_c_2));
  ONE_BIT_ALU one_bit_alu_13 (
    .CNTRL({CNTRL[0], CNTRL[1], CNTRL[2], CNTRL[3], CNTRL[4], CNTRL[5], CNTRL[6]}), .C_2(one_bit_alu_13_c_2),
    .I(TO_AC[12]), .INPR(1'b0), .DR(DR[12]), .AC_i(AC[12]), .AC_i_1(AC[11]), .AC_i_1_2(AC[13]),
    .C(one_bit_alu_12_c_2));
  ONE_BIT_ALU one_bit_alu_14 (
    .CNTRL({CNTRL[0], CNTRL[1], CNTRL[2], CNTRL[3], CNTRL[4], CNTRL[5], CNTRL[6]}), .C_2(one_bit_alu_14_c_2),
    .I(TO_AC[13]), .INPR(1'b0), .DR(DR[13]), .AC_i(AC[13]), .AC_i_1(AC[12]), .AC_i_1_2(AC[14]),
    .C(one_bit_alu_13_c_2));
  ONE_BIT_ALU one_bit_alu_15 (
    .CNTRL({CNTRL[0], CNTRL[1], CNTRL[2], CNTRL[3], CNTRL[4], CNTRL[5], CNTRL[6]}), .C_2(one_bit_alu_15_c_2),
    .I(TO_AC[14]), .INPR(1'b0), .DR(DR[14]), .AC_i(AC[14]), .AC_i_1(AC[13]), .AC_i_1_2(AC[15]),
    .C(one_bit_alu_14_c_2));
  ONE_BIT_ALU one_bit_alu_16 (
    .CNTRL({CNTRL[0], CNTRL[1], CNTRL[2], CNTRL[3], CNTRL[4], CNTRL[5], CNTRL[6]}), .C_2(CARRY_OUT),
    .I(TO_AC[15]), .INPR(1'b0), .DR(DR[15]), .AC_i(AC[15]), .AC_i_1(AC[14]), .AC_i_1_2(E),
    .C(one_bit_alu_15_c_2));

  // Other names for the same wires on the sheet: AC_0_7[7:0] = AC[7:0]; AC_8_15[7:0] = AC[15:8];
  //   CNTRL_t[6:0] = {CNTRL[0], CNTRL[1], CNTRL[2], CNTRL[3], CNTRL[4], CNTRL[5], CNTRL[6]}; SHL = CNTRL[6];
  //   SHR = CNTRL[5]; COM = CNTRL[4]; INP_t = CNTRL[3]; DR_t = CNTRL[2]; ADD = CNTRL[1]; AND = CNTRL[0];
  //   DR_0_7[7:0] = DR[7:0]; DR_8_15[7:0] = DR[15:8]; INP_0_7[7:0] = INP; O0 = TO_AC[0]; OUT_0_7[7:0] = TO_AC[7:0];
  //   O1 = TO_AC[1]; O2 = TO_AC[2]; O3 = TO_AC[3]; O4 = TO_AC[4]; O5 = TO_AC[5]; O6 = TO_AC[6]; O7 = TO_AC[7];
  //   O8 = TO_AC[8]; OUT_8_15[7:0] = TO_AC[15:8]; O9 = TO_AC[9]; O10 = TO_AC[10]; O11 = TO_AC[11]; O12 = TO_AC[12];
  //   O13 = TO_AC[13]; O14 = TO_AC[14]; O15 = TO_AC[15]
endmodule

module ONE_BIT_ALU (
  input  INPR,
  input  DR,
  input  AC_i,
  input  AC_i_1,
  input  AC_i_1_2,
  input  C,
  input  [6:0] CNTRL,
  output C_2,
  output I
);

  wire full_adder_1_s;
  wire [6:0] out;

  full_adder full_adder_1 (.x(AC_i), .y(DR), .cIn(C), .s(full_adder_1_s), .cout(C_2));
  and and_1 (out[0], AC_i, DR, CNTRL[6]);
  and and_2 (out[1], CNTRL[5], full_adder_1_s);
  and and_3 (out[2], CNTRL[4], DR);
  and and_4 (out[3], CNTRL[3], INPR);
  and and_5 (out[4], CNTRL[2], ~AC_i);  // AND_Gate
  and and_6 (out[5], CNTRL[1], AC_i_1_2);
  and and_7 (out[6], AC_i_1, CNTRL[0]);
  or or_1 (I, out[0], out[1], out[2], out[3], out[4], out[5], out[6]);

  // Other names for the same wires on the sheet: SHL = CNTRL[0]; SHR = CNTRL[1]; COM = CNTRL[2]; INP = CNTRL[3];
  //   DR_t = CNTRL[4]; ADD = CNTRL[5]; AND = CNTRL[6]
endmodule

module I (
  input  Clock,
  input  IR_15,
  input  R,
  input  [15:0] TIME,
  output I
);

  wire and_1_out;

  and and_1 (and_1_out, ~R, TIME[3]);  // AND_Gate
  D_Flip_Flop d_ff_1 (.clk(Clock), .D(IR_15), .Q(I), .en(and_1_out));  // open: Qn, preset, reset
endmodule

module E (
  input  E_OUT_ALU,
  input  [15:0] IR,
  input  T3,
  input  Clock,
  input  I,
  output E
);

  wire and_1_out, and_2_out, and_3_out, and_4_out, and_5_out, D7, not_1_out, or_1_out, or_2_out, or_3_out;

  Decoder #(.select(3), .enable("false")) decoder_1 (
    .out7(D7), .sel(IR[14:12]));  // open: out0, out1, out2, out3, out4, out5, out6
  or or_1 (or_1_out, and_3_out, and_2_out);
  and and_1 (and_1_out, T3, D7, ~I);  // AND_Gate
  and and_2 (and_2_out, and_1_out, IR[8]);
  and and_3 (and_3_out, and_1_out, IR[10]);
  not not_1 (not_1_out, or_1_out);
  and and_4 (and_4_out, ~E_OUT_ALU, not_1_out);  // AND_Gate
  and and_5 (and_5_out, E_OUT_ALU, not_1_out);
  or or_2 (or_2_out, and_5_out, and_2_out);
  or or_3 (or_3_out, and_4_out, and_2_out, and_3_out);
  J_K_Flip_Flop j_k_ff_1 (.J(or_2_out), .clk(Clock), .K(or_3_out), .Q(E));  // open: Qn, preset, en, reset

  // Other names for the same wires on the sheet: B7 = IR[7]; B8 = IR[8]; B10 = IR[10]
endmodule

module R (
  input  FGO,
  input  FGI,
  input  IEN,
  input  Clock,
  input  [15:0] TIME,
  output R
);

  wire and_1_out, and_2_out, nor_1_out, or_1_out;

  or or_1 (or_1_out, FGO, FGI);
  nor nor_1 (nor_1_out, TIME[0], TIME[1], TIME[2]);
  and and_1 (and_1_out, or_1_out, IEN, nor_1_out);
  and and_2 (and_2_out, TIME[2], R);
  J_K_Flip_Flop j_k_ff_1 (.J(and_1_out), .clk(Clock), .K(and_2_out), .Q(R));  // open: Qn, preset, en, reset
endmodule

module FGI (
  input  [15:0] IR,
  input  T3,
  input  I,
  input  ClK,
  input  [7:0] INPR,
  output FGI
);

  wire and_1_out, decoder_1_out7, OR, p;

  Decoder #(.select(3), .enable("false")) decoder_1 (
    .out7(decoder_1_out7), .sel(IR[14:12]));  // open: out0, out1, out2, out3, out4, out5, out6
  and and_1 (and_1_out, p, IR[11]);
  J_K_Flip_Flop j_k_ff_1 (.J(OR), .clk(ClK), .K(and_1_out), .Q(FGI));  // open: Qn, preset, en, reset
  or or_1 (OR, INPR[7], INPR[7], INPR[7], INPR[7], INPR[3], INPR[2], INPR[1], INPR[0]);
  and and_2 (p, T3, decoder_1_out7, I);

  assign INPR[6:4] = {3{INPR[7]}};

  // Other names for the same wires on the sheet: B11 = IR[11]
endmodule

module FGO (
  input  [15:0] IR,
  input  T3,
  input  I,
  input  ClK,
  input  [7:0] OUTR,
  output FGO
);

  wire and_1_out, decoder_1_out7, OR, p;

  Decoder #(.select(3), .enable("false")) decoder_1 (
    .out7(decoder_1_out7), .sel(IR[14:12]));  // open: out0, out1, out2, out3, out4, out5, out6
  and and_1 (and_1_out, p, IR[11]);
  J_K_Flip_Flop j_k_ff_1 (.J(OR), .clk(ClK), .K(and_1_out), .Q(FGO));  // open: Qn, preset, en, reset
  or or_1 (OR, OUTR[7], OUTR[7], OUTR[7], OUTR[7], OUTR[3], OUTR[2], OUTR[1], OUTR[0]);
  and and_2 (p, T3, decoder_1_out7, I);

  assign OUTR[6:4] = {3{OUTR[7]}};

  // Other names for the same wires on the sheet: B11 = IR[11]
endmodule

module IEN (
  input  [15:0] IR,
  input  ClK,
  input  R,
  input  T2,
  input  T3,
  input  I,
  output IEN
);

  wire and_1_out, and_2_out, and_3_out, and_4_out, decoder_1_out7, or_1_out;

  Decoder #(.select(3), .enable("false")) decoder_1 (
    .out7(decoder_1_out7), .sel(IR[14:12]));  // open: out0, out1, out2, out3, out4, out5, out6
  and and_1 (and_1_out, T3, decoder_1_out7, I);
  and and_2 (and_2_out, and_1_out, IR[6]);
  and and_3 (and_3_out, and_1_out, IR[7]);
  and and_4 (and_4_out, R, T2);
  or or_1 (or_1_out, and_4_out, and_2_out);
  J_K_Flip_Flop j_k_ff_1 (.J(and_3_out), .clk(ClK), .K(or_1_out), .Q(IEN));  // open: Qn, preset, en, reset
endmodule

module OUTR (
  input  LD_OUTR,
  input  ClK,
  input  [15:0] INPUT,
  output [7:0] OUTPUT
);

  Counter counter_1 (.load(LD_OUTR), .D(INPUT[7:0]), .count(1'b0), .Q(OUTPUT), .clk(ClK));  // open: carry, clr
endmodule

module S (
  input  [15:0] IR,
  input  T3,
  input  I,
  input  ClK,
  output S
);

  wire and_1_out, decoder_1_out7, r;

  Decoder #(.select(3), .enable("false")) decoder_1 (
    .out7(decoder_1_out7), .sel(IR[14:12]));  // open: out0, out1, out2, out3, out4, out5, out6
  and and_1 (and_1_out, r, IR[0]);
  J_K_Flip_Flop j_k_ff_1 (.J(and_1_out), .clk(ClK), .K(1'b0), .Q(S));  // open: Qn, preset, en, reset
  and and_2 (r, T3, decoder_1_out7, ~I);  // AND_Gate

  // Other names for the same wires on the sheet: B0 = IR[0]
endmodule

module AC_CNTRL (
  input  in_1,
  input  [15:0] IR,
  input  T3,
  input  I,
  output LD_AC,
  output [6:0] CTRL,
  output INR_AC,
  output CLR_AC
);

  wire D0, D1, D2, decoder_1_out7, p, r;

  and AND (CTRL[0], D0, in_1);
  and ADD (CTRL[1], in_1, D1);
  and DR (CTRL[2], in_1, D2);
  and INPR (CTRL[3], p, IR[11]);
  and COM (CTRL[4], r, IR[9]);
  and SHR (CTRL[5], r, IR[7]);
  and SHL (CTRL[6], r, IR[6]);
  and INC (INR_AC, r, IR[5]);
  and CLR (CLR_AC, r, IR[11]);
  Decoder #(.select(3), .enable("false")) decoder_1 (
    .out0(D0), .out1(D1), .out2(D2), .out7(decoder_1_out7), .sel(IR[14:12]));  // open: out3, out4, out5, out6
  and and_2 (r, T3, decoder_1_out7, ~I);  // AND_Gate
  and and_3 (p, T3, decoder_1_out7, I);
  or or_1 (LD_AC, CTRL[0], CTRL[1], CTRL[2], CTRL[3], CTRL[4], CTRL[5], CTRL[6]);

  // Other names for the same wires on the sheet: B0 = IR[0]; B5 = IR[5]; B6 = IR[6]; B7 = IR[7]; B9 = IR[9];
  //   B11 = IR[11]; T5 = in_1
endmodule

module SC_CNTRL (
  input  R,
  input  [15:0] IR,
  input  I,
  input  CLK,
  output [15:0] out_5,
  output [3:0] out_6
);

  wire and_3_out, and_4_out, and_5_out, and_6_out, and_7_out, and_8_out, and_9_out, and_10_out, D0, D1, D2,
       D3, D4, D5, D6, decoder_1_out7, decoder_2_out3, not_1_out, p, r_t, T, T2, T4, T5, T6;

  Decoder #(.select(3), .enable("false")) decoder_1 (
    .out0(D0), .out1(D1), .out2(D2), .out3(D3), .out4(D4), .out5(D5), .out6(D6), .out7(decoder_1_out7),
    .sel(IR[14:12]));
  not not_1 (not_1_out, T);
  and and_1 (r_t, decoder_2_out3, decoder_1_out7, ~I);  // AND_Gate
  and and_2 (p, decoder_2_out3, decoder_1_out7, I);
  Decoder #(.select(4)) decoder_2 (
    .out2(T2), .out3(decoder_2_out3), .out4(T4), .out5(T5), .out6(T6), .sel(out_6));  // open: out0, out1, out7, out8, out9, out10, out11, out12, out13, out14, out15, en
  Counter #(.width(4), .max('hf)) counter_1 (
    .load(T), .D(4'b0000), .count(not_1_out), .Q(out_6), .clk(CLK));  // open: carry, clr
  Decoder #(.select(4)) decoder_3 (
    .out0(out_5[0]), .out1(out_5[1]), .out2(out_5[2]), .out3(out_5[3]), .out4(out_5[4]), .out5(out_5[5]),
    .out6(out_5[6]), .out7(out_5[7]), .out8(out_5[8]), .out9(out_5[9]), .out10(out_5[10]), .out11(out_5[11]),
    .out12(out_5[12]), .out13(out_5[13]), .out14(out_5[14]), .out15(out_5[15]), .sel(out_6));  // open: en
  and and_3 (and_3_out, D0, T5);
  and and_4 (and_4_out, R, T2);
  and and_5 (and_5_out, D1, T5);
  and and_6 (and_6_out, D2, T5);
  and and_7 (and_7_out, D3, T4);
  and and_8 (and_8_out, D4, T4);
  and and_9 (and_9_out, D5, T5);
  and and_10 (and_10_out, D6, T6);
  or or_1 (T, and_3_out, and_4_out, and_5_out, and_6_out, and_7_out, and_8_out, and_9_out, and_10_out, r_t, p);
endmodule

module M_CNTRL (
  input  [15:0] IR,
  input  I,
  input  R,
  input  [3:0] in_4,
  output M_WR,
  output M_RD
);

  wire and_3_out, and_4_out, and_5_out, and_6_out, and_7_out, and_8_out, and_9_out, and_10_out, and_11_out,
       and_12_out, D0, D1, D2, D3, D4, D5, D6, D7, not_1_out, not_2_out, p, r_t, T1, T3, T4, T6;

  Decoder #(.select(4)) decoder_1 (
    .out1(T1), .out3(T3), .out4(T4), .out6(T6), .sel(in_4));  // open: out0, out2, out5, out7, out8, out9, out10, out11, out12, out13, out14, out15, en
  Decoder #(.select(3), .enable("false")) decoder_2 (
    .out0(D0), .out1(D1), .out2(D2), .out3(D3), .out4(D4), .out5(D5), .out6(D6), .out7(D7), .sel(IR[14:12]));
  and and_1 (r_t, T3, D7, ~I);  // AND_Gate
  and and_2 (p, T3, D7, I);
  not not_1 (not_1_out, R);
  not not_2 (not_2_out, D7);
  and and_3 (and_3_out, R, T1);
  and and_4 (and_4_out, D3, T4);
  and and_5 (and_5_out, D5, T4);
  and and_6 (and_6_out, D6, T6);
  and and_7 (and_7_out, not_1_out, T1);
  and and_8 (and_8_out, D0, T4);
  and and_9 (and_9_out, D1, T4);
  and and_10 (and_10_out, D2, T4);
  and and_11 (and_11_out, I, not_2_out, T3);
  and and_12 (and_12_out, D6, T4);
  or or_1 (M_WR, and_3_out, and_4_out, and_5_out, and_6_out);
  or or_2 (M_RD, and_7_out, and_8_out, and_9_out, and_10_out, and_11_out, and_12_out);
endmodule

module OUT_CNTRL (
  input  [15:0] IR,
  input  T3,
  input  I,
  output LOAD
);

  wire and_1_out, decoder_1_out7;

  Decoder #(.select(3), .enable("false")) decoder_1 (
    .out7(decoder_1_out7), .sel(IR[14:12]));  // open: out0, out1, out2, out3, out4, out5, out6
  and and_1 (and_1_out, T3, decoder_1_out7, I);
  and and_2 (LOAD, and_1_out, IR[10]);

  // Other names for the same wires on the sheet: B10 = IR[10]
endmodule

module DR_CNTRL (
  input  T4,
  input  T5,
  input  [15:0] IR,
  input  T3,
  input  I,
  output LOAD,
  output INR
);

  wire and_3_out, and_4_out, and_5_out, and_6_out, D0, D1, D2, D6, decoder_1_out7, p, r;

  Decoder #(.select(3), .enable("false")) decoder_1 (
    .out0(D0), .out1(D1), .out2(D2), .out6(D6), .out7(decoder_1_out7), .sel(IR[14:12]));  // open: out3, out4, out5
  and and_1 (r, T3, decoder_1_out7, ~I);  // AND_Gate
  and and_2 (p, T3, decoder_1_out7, I);
  and and_3 (and_3_out, D0, T4);
  and and_4 (and_4_out, D1, T4);
  and and_5 (and_5_out, D2, T4);
  and and_6 (and_6_out, D6, T4);
  and and_7 (INR, D6, T5);
  or or_1 (LOAD, and_3_out, and_4_out, and_5_out, and_6_out);

  // Other names for the same wires on the sheet: B0 = IR[0]; B5 = IR[5]; B6 = IR[6]; B7 = IR[7]; B9 = IR[9];
  //   B11 = IR[11]
endmodule

module AR_CNTRL (
  input  [15:0] IR,
  input  I,
  input  R,
  input  [15:0] T,
  output LD_AR,
  output INR_AR,
  output CLR_AR
);

  wire and_3_out, and_4_out, and_5_out, D0, D1, D2, D3, D4, D5, D6, D7, p, r_t;

  Decoder #(.select(3), .enable("false")) decoder_1 (
    .out0(D0), .out1(D1), .out2(D2), .out3(D3), .out4(D4), .out5(D5), .out6(D6), .out7(D7), .sel(IR[14:12]));
  and and_1 (r_t, T[3], D7, ~I);  // AND_Gate
  and and_2 (p, T[3], D7, I);
  and and_3 (and_3_out, T[0], ~R);  // AND_Gate
  and and_4 (and_4_out, T[2], ~R);  // AND_Gate
  and and_5 (and_5_out, I, T[3], ~D7);  // AND_Gate
  and and_6 (CLR_AR, R, T[0]);
  or or_1 (LD_AR, and_3_out, and_4_out, and_5_out);
  and and_7 (INR_AR, D5, T[4]);
endmodule

module BUS_CNTRL (
  input  [15:0] IR,
  input  I,
  input  R,
  input  [15:0] T,
  output [2:0] Select
);

  wire and_3_out, and_4_out, and_5_out, and_6_out, and_7_out, and_8_out, and_9_out, and_10_out, and_11_out,
       and_12_out, and_13_out, and_14_out, and_15_out, and_16_out, and_17_out, and_18_out, and_19_out, D0,
       D1, D2, D3, D4, D5, D6, D7, not_1_out, not_2_out, not_3_out, not_4_out, or_1_out, or_2_out, or_3_out,
       or_4_out, or_5_out, p, r_t;

  Decoder #(.select(3), .enable("false")) decoder_1 (
    .out0(D0), .out1(D1), .out2(D2), .out3(D3), .out4(D4), .out5(D5), .out6(D6), .out7(D7), .sel(IR[14:12]));
  and and_1 (r_t, T[3], D7, ~I);  // AND_Gate
  and and_2 (p, T[3], D7, I);
  not not_1 (not_1_out, D7);
  not not_2 (not_2_out, R);
  not not_3 (not_3_out, R);
  and and_3 (and_3_out, R, T[1]);
  not not_4 (not_4_out, R);
  and and_4 (and_4_out, not_4_out, T[1]);
  and and_5 (and_5_out, D0, T[4]);
  and and_6 (and_6_out, D1, T[4]);
  and and_7 (and_7_out, D2, T[4]);
  and and_8 (and_8_out, D6, T[4]);
  and and_9 (and_9_out, not_1_out, I, T[3]);
  and and_10 (and_10_out, T[4], D4);
  and and_11 (and_11_out, T[5], D5);
  and and_12 (and_12_out, not_2_out, T[0]);
  and and_13 (and_13_out, T[4], D5);
  and and_14 (and_14_out, R, T[0]);
  and and_15 (and_15_out, T[5], D2);
  and and_16 (and_16_out, T[6], D6);
  and and_17 (and_17_out, T[4], D3);
  and and_18 (and_18_out, p, IR[10]);
  and and_19 (and_19_out, not_3_out, T[2]);
  or or_1 (or_1_out, and_10_out, and_11_out);
  or or_2 (or_2_out, and_12_out, and_13_out, and_14_out);
  or or_3 (or_3_out, and_15_out, and_16_out);
  or or_4 (or_4_out, and_17_out, and_18_out);
  or or_5 (or_5_out, and_4_out, and_5_out, and_6_out, and_9_out, and_7_out, and_8_out, r_t);
  Priority_Encoder priority_encoder_1 (
    .in0(1'b0), .in1(or_1_out), .in2(or_2_out), .in3(or_3_out), .in4(or_4_out), .in5(and_19_out),
    .in6(and_3_out), .in7(or_5_out), .out(Select));  // open: en_in, gs, en_out

  // Other names for the same wires on the sheet: B10 = IR[10]
endmodule

module PC_CNTRL1 (
  input  [15:0] DR,
  input  [15:0] IR,
  input  [15:0] AC,
  input  I,
  input  E,
  input  FGI,
  input  FGO,
  input  R,
  input  [15:0] T,
  output INR,
  output CLR,
  output LD
);

  wire and_3_out, and_4_out, and_5_out, and_6_out, and_7_out, and_8_out, and_9_out, and_10_out, and_11_out,
       and_13_out, and_14_out, D0, D1, D2, D3, D4, D5, D6, D7, not_1_out, not_2_out, not_3_out, not_4_out,
       not_5_out, or_1_out, or_2_out, p, r_t;

  Decoder #(.select(3), .enable("false")) decoder_1 (
    .out0(D0), .out1(D1), .out2(D2), .out3(D3), .out4(D4), .out5(D5), .out6(D6), .out7(D7), .sel(IR[14:12]));
  and and_1 (r_t, T[3], D7, ~I);  // AND_Gate
  and and_2 (p, T[3], D7, I);
  or or_1 (or_1_out, AC[15], AC[14], AC[13], AC[12], AC[11], AC[10], AC[9], AC[8], AC[6], AC[5], AC[4], AC[3], AC[2], AC[1], AC[0], AC[7]);
  or or_2 (or_2_out, DR[15], DR[14], DR[13], DR[12], DR[11], DR[10], DR[9], DR[8], DR[6], DR[5], DR[4], DR[3], DR[2], DR[1], DR[0], DR[7]);
  not not_1 (not_1_out, or_1_out);
  not not_2 (not_2_out, R);
  not not_3 (not_3_out, or_2_out);
  not not_4 (not_4_out, AC[15]);
  not not_5 (not_5_out, E);
  and and_3 (and_3_out, not_2_out, T[1]);
  and and_4 (and_4_out, R, T[2]);
  and and_5 (and_5_out, D6, T[6], not_3_out);
  and and_6 (and_6_out, r_t, IR[4], not_4_out);
  and and_7 (and_7_out, r_t, IR[3], AC[15]);
  and and_8 (and_8_out, r_t, IR[2], not_1_out);
  and and_9 (and_9_out, r_t, IR[1], not_5_out);
  and and_10 (and_10_out, p, IR[9], FGI);
  and and_11 (and_11_out, p, FGO);
  and and_12 (CLR, R, T[1]);
  and and_13 (and_13_out, D4, T[4]);
  and and_14 (and_14_out, D5, T[5]);
  or or_3 (LD, and_13_out, and_14_out);
  or or_4 (INR, and_3_out, and_4_out, and_5_out, and_6_out, and_7_out, and_8_out, and_9_out, and_10_out, and_11_out);

  // Other names for the same wires on the sheet: B0 = IR[0]; B1 = IR[1]; B2 = IR[2]; B3 = IR[3]; B4 = IR[4];
  //   B5 = IR[5]; B6 = IR[6]; B7 = IR[7]; B8 = IR[8]; B9 = IR[9]; B10 = IR[10]; B11 = IR[11]
endmodule
